# Fritzing sketch Bluetooth with LED (saved by Fritzing 0.9.3b)
breadboards: 1

parts:
  Part1 = Bluetooth HC-05 Macho
  Part2 = Arduino Mega 2560 (Rev3)
  LED1 = LED - 5mm [color="Red (633nm)" package="5 mm [THT]"]
  R1 = Resistor [tolerance=±5% resistance=220 package=THT]

nets:
  N1: Part1.TXD, Part2.D0_RX0
  N2: Part1.RXD, Part2.D1_TX0
  VCC: Part1.VCC, Part2.5V
  GND: Part1.GND, Part2.GND, LED1.cathode
  N3: Part2.D7_PWM, R1.Pin_1
  N4: LED1.anode, R1.Pin_0

// code stored in the sketch: Bluetooth with LED.ino
int val;
void setup() {
  pinMode(7, OUTPUT); //Positive Terminal of LED
 
  Serial.begin(9600); 
}
 
void loop() { 
  digitalWrite(8, LOW); //Allways LOW
  
  //Read input from bluetooth module:
  if( Serial.available()){
    val = Serial.read();
  }
  
  //Input key switch
    switch(val){
      case '0':    
        digitalWrite(10, LOW);  //LED OFF
        break;
      case '1':  
        digitalWrite(10, HIGH); //LED ON
        break;
      default:
        break;  // default code (should never run)
    }
}
