# Fritzing sketch DHT with LCD and Ultrasonic sensor (saved by Fritzing 0.9.3b)
breadboards: 1

parts:
  Part3 = Arduino Mega 2560 (Rev3)
  LCD3 = LCD screen
  R6 = Rotary Potentiometer (Small) [maximum_resistance=100kΩ package=THT]
  R7 = Resistor [tolerance=±5% resistance=220 package=THT]
  DHT2 = DHT11 Humitidy and Temperature Sensor
  R8 = Resistor [tolerance=±5% resistance=220 package=THT]
  hc-sr1 = hc-sr04

nets:
  GND: Part3.GND, LCD3.VSS, LCD3.R/W, LCD3.LED-, R6.leg2, DHT2.GND, hc-sr1.GND
  N1: Part3.D11_PWM, LCD3.E
  N2: Part3.D10_PWM, hc-sr1.Trig
  N3: Part3.D9_PWM, hc-sr1.Echo
  VDD: Part3.5V, LCD3.VDD, R6.leg1, R7.Pin_0, DHT2.VDD, R8.Pin_1, hc-sr1.VCC
  N4: Part3.D2_PWM, LCD3.DB7
  N5: Part3.D3_PWM, LCD3.DB6
  N6: Part3.D4_PWM, LCD3.DB5
  N7: Part3.D5_PWM, LCD3.DB4
  N8: Part3.D7_PWM, DHT2.DATA, R8.Pin_0
  N9: LCD3.V0, R6.wiper
  N10: LCD3.LED+, R7.Pin_1

custom parts:
  DHT11 Humitidy and Temperature Sensor: DHT11 Humidity and Temperature Sensor

// code stored in the sketch: DHT with LCD and Ultrasonic sensor.ino
#include <dht.h>
#include <LiquidCrystal.h>

LiquidCrystal lcd(12, 11, 5, 4, 3, 2);

dht DHT;

#define DHT11_PIN 7

const int trigPin = 10;
const int echoPin = 9;
long duration;
int distanceCm, distanceInch;

void setup(){
  lcd.begin(16, 2);
  pinMode(trigPin, OUTPUT);
  pinMode(echoPin, INPUT);
}

void loop()
{

	digitalWrite(trigPin, LOW);
  delayMicroseconds(2);
  digitalWrite(trigPin, HIGH);
  delayMicroseconds(10);
  digitalWrite(trigPin, LOW);

duration = pulseIn(echoPin, HIGH);
distanceCm= duration*0.034/2;
distanceInch = duration*0.0133/2;

lcd.setCursor(0,0); // Sets the location at which subsequent text written to the LCD will be displayed
lcd.print("Distance: "); // Prints string "Distance" on the LCD
lcd.print(distanceCm); // Prints the distance value from the sensor
lcd.print("cm");
delay(10)
	
  int chk = DHT.read11(DHT11_PIN);
  lcd.setCursor(0,0); 
  lcd.print("Temp: ");
  lcd.print(DHT.temperature);
  lcd.print((char)223);
  lcd.print("C");
  lcd.setCursor(0,1);
  lcd.print("Hum: ");
  lcd.print(DHT.humidity);
  lcd.print("%");
  delay(1000);
}
