# Fritzing sketch DHT11 with LCD (saved by Fritzing 0.9.3b)
breadboards: 1

parts:
  Part2 = Arduino Mega 2560 (Rev3)
  LCD2 = LCD screen
  R3 = Rotary Potentiometer (Small) [maximum_resistance=100kΩ package=THT]
  R4 = Resistor [tolerance=±5% resistance=220 package=THT]
  DHT1 = DHT11 Humitidy and Temperature Sensor
  R5 = Resistor [tolerance=±5% resistance=220 package=THT]

nets:
  GND: Part2.GND, LCD2.VSS, LCD2.R/W, LCD2.LED-, R3.leg2, DHT1.GND
  N1: Part2.D11_PWM, LCD2.E
  VDD: Part2.3V3, LCD2.VDD, R3.leg1, R4.Pin_0, DHT1.VDD, R5.Pin_1
  N2: Part2.D2_PWM, LCD2.DB7
  N3: Part2.D3_PWM, LCD2.DB6
  N4: Part2.D4_PWM, LCD2.DB5
  N5: Part2.D5_PWM, LCD2.DB4
  N6: LCD2.V0, R3.wiper
  N7: LCD2.LED+, R4.Pin_1
  N8: DHT1.DATA, R5.Pin_0

custom parts:
  DHT11 Humitidy and Temperature Sensor: DHT11 Humidity and Temperature Sensor

// code stored in the sketch: DHT11 with LCD.ino
#include <dht.h>
#include <LiquidCrystal.h>

LiquidCrystal lcd(12, 11, 5, 4, 3, 2);

dht DHT;

#define DHT11_PIN 7

void setup(){
  lcd.begin(16, 2);
}

void loop()
{
  int chk = DHT.read11(DHT11_PIN);
  lcd.setCursor(0,0); 
  lcd.print("Temp: ");
  lcd.print(DHT.temperature);
  lcd.print((char)223);
  lcd.print("C");
  lcd.setCursor(0,1);
  lcd.print("Humidity: ");
  lcd.print(DHT.humidity);
  lcd.print("%");
  delay(1000);
}
