# Fritzing sketch Keypad with LCD (saved by Fritzing 0.9.3b)

parts:
  Matrix_keypad1 = KEYPAD 4x4
  Part1 = Arduino Mega 2560 (Rev3)
  U1 = LCD-16X2 [package=lcd-16x2]

nets (from the schematic view):
  N1: Matrix_keypad1.col1, Part1.D9_PWM
  N2: Matrix_keypad1.col2, Part1.D8_PWM
  N3: Matrix_keypad1.col3, Part1.D7_PWM
  N4: Matrix_keypad1.col4, Part1.D6_PWM
  N5: Matrix_keypad1.row1, Part1.D5_PWM
  N6: Matrix_keypad1.row2, Part1.D4_PWM
  N7: Matrix_keypad1.row3, Part1.D3_PWM
  N8: Matrix_keypad1.row4, Part1.D2_PWM
  N9: Part1.D12_PWM, U1.RS
  N10: Part1.D11_PWM, U1.E
  5V: Part1.5V, U1.VSS
  N11: Part1.GND, U1.R_W
  N12: Part1.D45, U1.DB4
  N13: Part1.D47, U1.DB5
  N14: Part1.D49, U1.DB6
  N15: Part1.D51, U1.DB7

custom parts:
  KEYPAD 4x4: Matrix keypad 16 buttons, 4 rows x 4 columns

// code stored in the sketch: Keypad with LCD..ino
#include <Wire.h> 
#include <LiquidCrystal.h>
#include <Keypad.h>

LiquidCrystal lcd(12, 11, 45, 47, 49, 51);

const byte ROWS = 4;
const byte COLS = 4;

char hexaKeys[ROWS][COLS] = {
  {'1', '2', '3', 'A'},
  {'4', '5', '6', 'B'},
  {'7', '8', '9', 'C'},
  {'*', '0', '#', 'D'}
};

byte rowPins[ROWS] = {9, 8, 7, 6};
byte colPins[COLS] = {5, 4, 3, 2};

Keypad customKeypad = Keypad(makeKeymap(hexaKeys), rowPins, colPins, ROWS, COLS);

 

void setup(){
  lcd.backlight();
  lcd.init(); 
}

void loop(){
  char customKey = customKeypad.getKey();
  if (customKey){
    lcd.clear();
    lcd.setCursor(0, 0); 
    lcd.print(customKey);
  }
}
