# Fritzing sketch Keypad with serial (saved by Fritzing 0.9.3b)

parts:
  Part2 = Arduino Mega 2560 (Rev3)
  Matrix_keypad2 = KEYPAD 4x4

nets:
  N1: Part2.D9_PWM, Matrix_keypad2.col1
  N2: Part2.D8_PWM, Matrix_keypad2.col2
  N3: Part2.D2_PWM, Matrix_keypad2.row4
  N4: Part2.D3_PWM, Matrix_keypad2.row3
  N5: Part2.D4_PWM, Matrix_keypad2.row2
  N6: Part2.D5_PWM, Matrix_keypad2.row1
  N7: Part2.D6_PWM, Matrix_keypad2.col4
  N8: Part2.D7_PWM, Matrix_keypad2.col3

custom parts:
  KEYPAD 4x4: Matrix keypad 16 buttons, 4 rows x 4 columns

// code stored in the sketch: Keypad with serial.ino
#include <Keypad.h>

const byte ROWS = 4; 
const byte COLS = 4; 

char hexaKeys[ROWS][COLS] = {
  {'1', '2', '3', 'A'},
  {'4', '5', '6', 'B'},
  {'7', '8', '9', 'C'},
  {'*', '0', '#', 'D'}
};

byte rowPins[ROWS] = {9, 8, 7, 6}; 
byte colPins[COLS] = {5, 4, 3, 2}; 

Keypad customKeypad = Keypad(makeKeymap(hexaKeys), rowPins, colPins, ROWS, COLS); 

void setup(){
  Serial.begin(9600);
}
  
void loop(){
  char customKey = customKeypad.getKey();
  
  if (customKey){
    Serial.println(customKey);
  }
}
