# Fritzing sketch LCD HelloWorld (saved by Fritzing 0.9.3b)
breadboards: 1

parts:
  Part1 = Arduino Mega 2560 (Rev3)
  LCD1 = LCD screen
  R1 = Rotary Potentiometer (Small) [maximum_resistance=100kΩ package=THT]
  R2 = Resistor [tolerance=±5% resistance=220 package=THT]

nets:
  GND: Part1.GND, LCD1.VSS, LCD1.R/W, LCD1.LED-, R1.leg2
  N1: Part1.D12_PWM, LCD1.RS
  N2: Part1.D11_PWM, LCD1.E
  3V3: Part1.3V3, LCD1.VDD, R1.leg1, R2.Pin_0
  N3: Part1.D2_PWM, LCD1.DB7
  N4: Part1.D3_PWM, LCD1.DB6
  N5: Part1.D4_PWM, LCD1.DB5
  N6: Part1.D5_PWM, LCD1.DB4
  N7: LCD1.V0, R1.wiper
  N8: LCD1.LED+, R2.Pin_1

// code stored in the sketch: LCD HelloWorld.ino
// include the library code:
#include <LiquidCrystal.h>

// initialize the library by associating any needed LCD interface pin
// with the arduino pin number it is connected to
const int rs = 12, en = 11, d4 = 5, d5 = 4, d6 = 3, d7 = 2;
LiquidCrystal lcd(rs, en, d4, d5, d6, d7);

void setup() {
  // set up the LCD's number of columns and rows:
  lcd.begin(16, 2);
  // Print a message to the LCD.
  lcd.print("hello, world!");
}

void loop() {
  // set the cursor to column 0, line 1
  // (note: line 1 is the second row, since counting begins with 0):
  lcd.setCursor(0, 1);
  // print the number of seconds since reset:
  lcd.print(millis() / 1000);
}
