# Fritzing sketch LCD with Ultrasonic sensor (saved by Fritzing 0.9.3b)
breadboards: 1

parts:
  Part1 = Arduino Mega 2560 (Rev3)
  hc-sr1 = hc-sr04
  LCD1 = LCD screen
  R1 = Rotary Potentiometer (Small) [maximum_resistance=100kΩ package=THT]
  R2 = Resistor [tolerance=±5% resistance=220 package=THT]

nets:
  GND: Part1.GND, hc-sr1.GND, LCD1.VSS, LCD1.R/W, LCD1.LED-, R1.leg2
  N1: Part1.D12_PWM, LCD1.E
  N2: Part1.D11_PWM, LCD1.RS
  N3: Part1.D9_PWM, hc-sr1.Echo
  N4: Part1.D8_PWM, hc-sr1.Trig
  5V: Part1.5V, hc-sr1.VCC, LCD1.VDD, R1.leg1, R2.Pin_0
  N5: Part1.D2_PWM, LCD1.DB7
  N6: Part1.D3_PWM, LCD1.DB6
  N7: Part1.D4_PWM, LCD1.DB5
  N8: Part1.D5_PWM, LCD1.DB4
  N9: LCD1.V0, R1.wiper
  N10: LCD1.LED+, R2.Pin_1

// code stored in the sketch: LCD with Ultrasonic sensor.ino
/*
* Ultrasonic Sensor HC-SR04 and LCD 
*
* by Isaac Mwondi
*
*/
#include <LiquidCrystal.h> // includes the LiquidCrystal Library

LiquidCrystal lcd(12, 11, 5, 4, 3, 2); // Creates an LCD object. Parameters: (rs, enable, d4, d5, d6, d7)

const int trigPin = 9;
const int echoPin = 10;
long duration;
int distanceCm, distanceInch;

void setup() {
lcd.begin(16,2); // Initializes the interface to the LCD screen, and specifies the dimensions (width and height) of the display
pinMode(trigPin, OUTPUT);
pinMode(echoPin, INPUT);
}

void loop() {
digitalWrite(trigPin, LOW);
delayMicroseconds(2);
digitalWrite(trigPin, HIGH);
delayMicroseconds(10);
digitalWrite(trigPin, LOW);

duration = pulseIn(echoPin, HIGH);
distanceCm= duration*0.034/2;
distanceInch = duration*0.0133/2;

lcd.setCursor(0,0); // Sets the location at which subsequent text written to the LCD will be displayed
lcd.print("Distance: "); // Prints string "Distance" on the LCD
lcd.print(distanceCm); // Prints the distance value from the sensor
lcd.print(" cm");
delay(10);

lcd.setCursor(0,1);
lcd.print("Distance: ");
lcd.print(distanceInch);
lcd.print(" inch");
delay(10);
}
