# Fritzing sketch Pull down resistor (saved by Fritzing 0.9.3b)
breadboards: 1

parts:
  Part1 = Arduino Mega 2560 (Rev3)
  S1 = Pushbutton [package="[THT]"]
  LED1 = LED - 5mm [color="Red (633nm)" package="5 mm [THT]"]
  R1 = Resistor [tolerance=±5% resistance=220 package=THT]
  R2 = Resistor [tolerance=±5% resistance=220 package=THT]

nets:
  N1: Part1.GND, R1.Pin_1
  N2: Part1.D9_PWM, LED1.anode
  N3: Part1.5V, S1.Pin_3, S1.Pin_4
  N4: Part1.D4_PWM, S1.Pin_1, S1.Pin_2, R1.Pin_0
  N5: LED1.cathode, R2.Pin_1

notes:
  Default state is LOW
