# Fritzing sketch Pull up resistor (saved by Fritzing 0.9.3b)
breadboards: 1

parts:
  Part2 = Arduino Mega 2560 (Rev3)
  S2 = Pushbutton [package="[THT]"]
  LED2 = LED - 5mm [color="Red (633nm)" package="5 mm [THT]"]
  R3 = Resistor [tolerance=±5% resistance=220 package=THT]
  R4 = Resistor [tolerance=±5% resistance=220 package=THT]

nets:
  N1: Part2.GND, S2.Pin_3, S2.Pin_4, R3.Pin_1, R4.Pin_0
  N2: Part2.D9_PWM, LED2.anode
  N3: Part2.D4_PWM, S2.Pin_1, S2.Pin_2, R3.Pin_0
  N4: LED2.cathode, R4.Pin_1
