# Fritzing sketch Push Button (saved by Fritzing 0.9.3b)
breadboards: 1

parts:
  Part1 = Arduino Mega 2560 (Rev3)
  R1 = Resistor [tolerance=±5% resistance=220 package=THT]
  S1 = Pushbutton [package="[THT]"]  # not connected

nets:
  N1: Part1.GND, R1.Pin_1

// code stored in the sketch: Push Button.ino
//Push button to switch on and off built in led


const int buttonPin = 2;     // the number of the pushbutton pin


// variables will change:
int buttonState = 0;         // variable for reading the pushbutton status

void setup() {
  // initialize the LED pin as an output:
  pinMode(LED_BUILTIN, OUTPUT);
  // initialize the pushbutton pin as an input:
  pinMode(buttonPin, INPUT);
}

void loop() {
  // read the state of the pushbutton value:
  buttonState = digitalRead(buttonPin);

  // check if the pushbutton is pressed. If it is, the buttonState is HIGH:
  if (buttonState == HIGH) {
    // turn LED on:
    digitalWrite(LED_BUILTIN, HIGH);
  } else {
    // turn LED off:
    digitalWrite(LED_BUILTIN, LOW);
  }
}
