# Fritzing sketch Touch sensor with serial (saved by Fritzing 0.9.3b)

parts:
  TP1 = TTP223 Touch Module [part_number=TTP223]
  Part1 = Arduino Mega 2560 (Rev3)

nets:
  GND: TP1.GND, Part1.GND
  N1: TP1.I/O, Part1.D6_PWM
  VCC: TP1.VCC, Part1.5V

custom parts:
  TTP223 Touch Module: Single touch module. Other side has "A" "B" terminal to short and use "AHLB" & "Toggle" Mode.

// code stored in the sketch: Touch sensor with serial.ino
void setup()
{
pinMode(2, INPUT);
Serial.begin(9600);

}

void loop()
{

if (digitalRead(2)== HIGH);
Serial.println("Sensor is touched");
delay(500);
}
