# Fritzing sketch Wi-Fi module with serial (saved by Fritzing 0.9.3b)

parts:
  U1 = ESP8266 WiFi Module [part_number=ESP8266]
  Part1 = Arduino Mega 2560 (Rev3)

nets:
  N1: U1.RXD, Part1.D10_PWM
  VCC: U1.VCC, Part1.3V3
  N2: U1.CH_PD, Part1.5V
  GND: U1.GND, U1.REST, Part1.GND
  N3: U1.TXD, Part1.D11_PWM
