# Fritzing sketch moisture_serial_fritzing (saved by Fritzing 0.9.3b)

parts:
  부품1 = FC-28 Soil Hygrometer Module - Probe
  부품2 = FC-28 Soil Hygrometer Module
  Part1 = Arduino Mega 2560 (Rev3)

nets:
  N1: 부품1.POS, 부품2.POS
  N2: 부품1.NEG, 부품2.NEG
  VCC: 부품2.VCC, Part1.5V
  GND: 부품2.GND, Part1.GND
  N3: 부품2.AO, Part1.A0

custom parts:
  FC-28 Soil Hygrometer Module - Probe: The FC-28 is a soil hygrometer module that uses the Texas Instruments LM393 comparator chip to provide an analog measurement of soil humidity.
  FC-28 Soil Hygrometer Module: The FC-28 is a soil hygrometer module that uses the Texas Instruments LM393 comparator chip to provide an analog measurement of soil humidity. The digital output is high when soil moisture is over a certain threshold, as determined by adjusting the potentiometer.

// code stored in the sketch: moisture_serial_fritzing.fzz.ino

void setup() {

  Serial.begin(9600); 
 
}

void loop() {

  int a = analogRead(A0); 

  Serial.println(a);  

  delay(2000); 

}
