# Fritzing sketch ultrasonic sensor with serial (saved by Fritzing 0.9.3b)
breadboards: 1

parts:
  Part1 = Arduino Mega 2560 (Rev3)
  hc-sr1 = hc-sr04

nets:
  N1: Part1.D10_PWM, hc-sr1.Trig
  N2: Part1.D9_PWM, hc-sr1.Echo
  5V: Part1.5V, hc-sr1.VCC
  GND: Part1.GND, hc-sr1.GND

// code stored in the sketch: ultrasonic sensor with serial.ino
/*
* Ultrasonic Sensor HC-SR04 and Arduino Tutorial
*
* by Gearbox

*
*/
// defines pins numbers
const int trigPin = 9;
const int echoPin = 10;
// defines variables
long duration;
int distance;
void setup() {
pinMode(trigPin, OUTPUT); // Sets the trigPin as an Output
pinMode(echoPin, INPUT); // Sets the echoPin as an Input
Serial.begin(9600); // Starts the serial communication
}
void loop() {
// Clears the trigPin
digitalWrite(trigPin, LOW);
delayMicroseconds(2);
// Sets the trigPin on HIGH state for 10 micro seconds
digitalWrite(trigPin, HIGH);
delayMicroseconds(10);
digitalWrite(trigPin, LOW);
// Reads the echoPin, returns the sound wave travel time in microseconds
duration = pulseIn(echoPin, HIGH);
// Calculating the distance
distance= duration*0.034/2;
// Prints the distance on the Serial Monitor
Serial.print("Distance: ");
Serial.println(distance);
}
